# Fritzing sketch V1 (saved by Fritzing 0.8.7b)
breadboards: 1

parts:
  U1 = ESP8266 WiFi Module [part_number=ESP8266]
  DHT1 = DHT11 Humitidy and Temperature Sensor
  VCC1 = Battery
  Debugger1 = Debugger

nets:
  N1: U1.RXD, Debugger1.TX
  VCC: U1.VCC, DHT1.VDD, VCC1.+
  N2: U1.GPIO_2, DHT1.DATA
  GND: U1.GND, DHT1.GND, VCC1.-
  N3: U1.TXD, Debugger1.RX

custom parts:
  ESP8266 WiFi Module: Generic WiFi Module based on the ESP8266 with onboard PCB antenna and UART communications
  DHT11 Humitidy and Temperature Sensor: DHT11 Humidity and Temperature Sensor
