# Fritzing sketch V2 (saved by Fritzing 0.8.7b)
breadboards: 1

parts:
  Arduino_UNO = Arduino Uno (Rev3)
  DHT111 = DHT11 Humitidy and Temperature Sensor
  part = ESP8266 WiFi Module [part_number=ESP8266]

nets:
  N1: Arduino_UNO.D2, part.TXD
  N2: Arduino_UNO.D3_PWM, part.RXD
  N3: Arduino_UNO.D4, DHT111.DATA
  3V3: Arduino_UNO.3V3, DHT111.VDD, part.VCC
  GND: Arduino_UNO.GND, DHT111.GND, part.GND

custom parts:
  DHT11 Humitidy and Temperature Sensor: DHT11 Humidity and Temperature Sensor
  ESP8266 WiFi Module: Generic WiFi Module based on the ESP8266 with onboard PCB antenna and UART communications
