# Fritzing sketch V3_ESP8266 (saved by Fritzing 0.8.7b)
breadboards: 1

parts:
  part = ESP8266 WiFi Module [part_number=ESP8266]
  TTL-USB = Debugger

nets:
  N1: part.RXD, TTL-USB.TX
  N2: part.VCC, part.CH_PD, TTL-USB.3v
  GND: part.GPIO_0, part.GND, TTL-USB.GND
  N3: part.TXD, TTL-USB.RX

custom parts:
  ESP8266 WiFi Module: Generic WiFi Module based on the ESP8266 with onboard PCB antenna and UART communications
  Debugger: Need to get all of your Atlas Scientific equipment calibrated and running smoothly in the shortest amount of time? This Debugger is specially designed to have its pin outs match up directly with all of the Atlas Scientific Circuits. Just plug it into your bread board and your ready to go. • Rapid calibration and debugging • 2 different output voltages (3.3 and 5.0) • Header pins directly line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
