# Fritzing sketch V3_UNO (saved by Fritzing 0.8.7b)
breadboards: 1

parts:
  UNO = Arduino Uno (Rev3)
  DS18B20 = TEMPERATURE-SENSOR [package=to-92]
  part = ESP8266 WiFi Module [part_number=ESP8266]

nets:
  N1: UNO.D0/RX, part.TXD
  N2: UNO.D1/TX, part.RXD
  N3: UNO.D2, DS18B20.ADJ
  VCC: UNO.3V3, DS18B20.VCC, part.VCC, part.CH_PD
  GND: UNO.GND, DS18B20.GND, part.GND

custom parts:
  ESP8266 WiFi Module: Generic WiFi Module based on the ESP8266 with onboard PCB antenna and UART communications
